// Logisim project ALU.circ as structural Verilog: 3 circuits, main circuit 1bit_adder
module _1bit_adder (
  input  a,
  input  b,
  input  cin,
  output cout,
  output r
);

  wire and_1_out, and_2_out, and_3_out, and_4_out, and_5_out, and_6_out, and_7_out, not_1_out, not_2_out,
       not_3_out, not_4_out, not_5_out, not_6_out;

  and and_1 (and_1_out, b, cin);
  and and_2 (and_2_out, a, cin);
  and and_3 (and_3_out, a, b);
  not not_1 (not_1_out, a);
  not not_2 (not_2_out, b);
  not not_3 (not_3_out, a);
  not not_4 (not_4_out, cin);
  not not_5 (not_5_out, b);
  not not_6 (not_6_out, cin);
  or or_1 (cout, and_1_out, and_2_out, and_3_out);
  and and_4 (and_4_out, not_1_out, not_2_out, cin);
  and and_5 (and_5_out, not_3_out, b, not_4_out);
  and and_6 (and_6_out, a, not_5_out, not_6_out);
  and and_7 (and_7_out, a, b, cin);
  or or_2 (r, and_4_out, and_5_out, and_6_out, and_7_out);
endmodule

module _1bit_ALU (
  input  a,
  input  b,
  input  Binvert,
  input  cin,
  input  [1:0] op,
  output cout,
  output result
);

  wire and_1_out, multiplexer_1_out, n1bit_adder_1_r, not_1_out, or_1_out;

  not not_1 (not_1_out, b);
  Multiplexer #(.enable("false")) multiplexer_1 (.in0(b), .in1(not_1_out), .out(multiplexer_1_out), .sel(Binvert));
  _1bit_adder u_1bit_adder_1 (.a(a), .b(multiplexer_1_out), .cin(cin), .cout(cout), .r(n1bit_adder_1_r));
  and and_1 (and_1_out, a, b);
  or or_1 (or_1_out, a, b);
  Multiplexer #(.select(2), .enable("false")) multiplexer_2 (
    .in0(n1bit_adder_1_r), .in1(and_1_out), .in2(or_1_out), .out(result), .sel(op));  // open: in3
endmodule

module alu (
  input  [3:0] A,
  input  [3:0] B,
  input  [1:0] op,
  output [3:0] out_4
);

  wire Bnegate, decoder_1_out0, decoder_1_out2, decoder_1_out3, n1bit_alu_1_cout, n1bit_alu_2_cout,
       n1bit_alu_3_cout, or_1_out;
  wire [1:0] op_t;

  Decoder #(.select(2), .enable("false")) decoder_1 (
    .out0(decoder_1_out0), .out1(Bnegate), .out2(decoder_1_out2), .out3(decoder_1_out3), .sel(op));
  _1bit_ALU u_1bit_alu_1 (
    .a(A[0]), .b(B[0]), .Binvert(Bnegate), .cin(Bnegate), .op(op_t), .result(out_4[0]),
    .cout(n1bit_alu_1_cout));
  or or_1 (or_1_out, decoder_1_out0, Bnegate);
  _1bit_ALU u_1bit_alu_2 (
    .a(A[1]), .b(B[1]), .Binvert(Bnegate), .cin(n1bit_alu_1_cout), .op(op_t), .result(out_4[1]),
    .cout(n1bit_alu_2_cout));
  Priority_Encoder #(.select(2)) priority_encoder_1 (
    .in0(or_1_out), .in1(decoder_1_out2), .in2(decoder_1_out3), .out(op_t));  // open: in3, gs, en_out, en_in
  _1bit_ALU u_1bit_alu_3 (
    .a(A[2]), .b(B[2]), .Binvert(Bnegate), .cin(n1bit_alu_2_cout), .op(op_t), .result(out_4[2]),
    .cout(n1bit_alu_3_cout));
  _1bit_ALU u_1bit_alu_4 (
    .a(A[3]), .b(B[3]), .Binvert(Bnegate), .cin(n1bit_alu_3_cout), .op(op_t), .result(out_4[3]));  // open: cout
endmodule
