// Logisim project CRC.circ as structural Verilog: 2 circuits, main circuit divider
module divider (
  input  [3:0] A_3_0,
  input  [3:0] B_3_0,
  output [2:0] C_2_0,
  output D
);

  wire [2:0] xor_1_out;

  xor xor_1 (xor_1_out[0], A_3_0[0], B_3_0[0]);
  xor xor_2 (xor_1_out[1], A_3_0[1], B_3_0[1]);
  xor xor_3 (xor_1_out[2], A_3_0[2], B_3_0[2]);
  Multiplexer #(.width(3), .enable("false")) multiplexer_1 (
    .in0(A_3_0[2:0]), .in1(xor_1_out), .out(C_2_0), .sel(A_3_0[3]));

  assign D = A_3_0[3];
endmodule

module CRC (
  input  [7:0] A_7_0,
  input  [3:0] B_3_0,
  output [10:0] out_3
);

  wire [2:0] divider_1_c_2_0, divider_2_c_2_0, divider_3_c_2_0, divider_4_c_2_0, divider_5_c_2_0,
       divider_6_c_2_0, divider_7_c_2_0;

  divider divider_1 (.A_3_0(A_7_0[7:4]), .B_3_0(B_3_0), .C_2_0(divider_1_c_2_0), .D(out_3[10]));
  // Probe on {divider_1_c_2_0, A_7_0[3]}
  // Probe on divider_2_c_2_0
  divider divider_2 (.A_3_0({divider_1_c_2_0, A_7_0[3]}), .B_3_0(B_3_0), .C_2_0(divider_2_c_2_0), .D(out_3[9]));
  // Probe on {divider_2_c_2_0, A_7_0[2]}
  divider divider_3 (.A_3_0({divider_2_c_2_0, A_7_0[2]}), .B_3_0(B_3_0), .C_2_0(divider_3_c_2_0), .D(out_3[8]));
  // Probe on divider_3_c_2_0
  // Probe on {divider_3_c_2_0, A_7_0[1]}
  divider divider_4 (.A_3_0({divider_3_c_2_0, A_7_0[1]}), .B_3_0(B_3_0), .C_2_0(divider_4_c_2_0), .D(out_3[7]));
  // Probe on divider_4_c_2_0
  // Probe on {divider_4_c_2_0, A_7_0[0]}
  divider divider_5 (.A_3_0({divider_4_c_2_0, A_7_0[0]}), .B_3_0(B_3_0), .C_2_0(divider_5_c_2_0), .D(out_3[6]));
  // Probe on divider_5_c_2_0
  divider divider_6 (.A_3_0({divider_5_c_2_0, 1'b0}), .B_3_0(B_3_0), .C_2_0(divider_6_c_2_0), .D(out_3[5]));
  divider divider_7 (.A_3_0({divider_6_c_2_0, 1'b0}), .B_3_0(B_3_0), .C_2_0(divider_7_c_2_0), .D(out_3[4]));
  divider divider_8 (.A_3_0({divider_7_c_2_0, 1'b0}), .B_3_0(B_3_0), .C_2_0(out_3[2:0]), .D(out_3[3]));
  // Probe on out_3[2:0]
endmodule
