// Logisim project 4bit_sort.circ as structural Verilog: 4 circuits, main circuit 1bit_swap
module _1bit_swap (
  input  I1,
  input  I2,
  input  S,
  output O1,
  output O2
);

  wire and_1_out, and_2_out, and_3_out, and_4_out;

  and and_1 (and_1_out, I1, ~S);  // AND_Gate
  and and_2 (and_2_out, I2, S);
  and and_3 (and_3_out, I2, ~S);  // AND_Gate
  and and_4 (and_4_out, I1, S);
  or or_1 (O1, and_1_out, and_2_out);
  or or_2 (O2, and_3_out, and_4_out);
endmodule

module _4bit_swap (
  input  [3:0] I1,
  input  [3:0] I2,
  input  S,
  output [3:0] O1,
  output [3:0] O2
);

  _1bit_swap u_1bit_swap_1 (.I1(I1[0]), .I2(I2[0]), .S(S), .O1(O1[0]), .O2(O2[0]));
  _1bit_swap u_1bit_swap_2 (.I1(I1[1]), .I2(I2[1]), .S(S), .O1(O1[1]), .O2(O2[1]));
  _1bit_swap u_1bit_swap_3 (.I1(I1[2]), .I2(I2[2]), .S(S), .O1(O1[2]), .O2(O2[2]));
  _1bit_swap u_1bit_swap_4 (.I1(I1[3]), .I2(I2[3]), .S(S), .O1(O1[3]), .O2(O2[3]));
endmodule

module _4bit_cmp (
  input  [3:0] num1,
  input  [3:0] num2,
  output [3:0] smaller,
  output [3:0] greater
);

  wire comparator_1_gt;

  Comparator #(.width(4), .mode("unsigned")) comparator_1 (.a(num1), .b(num2), .gt(comparator_1_gt));  // open: eq, lt
  _4bit_swap u_4bit_swap_1 (.I1(num1), .I2(num2), .S(comparator_1_gt), .O1(smaller), .O2(greater));
endmodule

module _4bit_sort (
  input  [3:0] A,
  input  [3:0] B,
  input  [3:0] C,
  input  [3:0] D,
  output [3:0] _1,
  output [3:0] _2,
  output [3:0] _3,
  output [3:0] _4
);

  wire [3:0] n4bit_cmp_1_greater, n4bit_cmp_1_smaller, n4bit_cmp_2_greater, n4bit_cmp_2_smaller,
       n4bit_cmp_3_smaller, n4bit_cmp_4_greater, n4bit_cmp_4_smaller, n4bit_cmp_5_smaller;

  _4bit_cmp u_4bit_cmp_1 (.num1(A), .num2(B), .smaller(n4bit_cmp_1_smaller), .greater(n4bit_cmp_1_greater));
  _4bit_cmp u_4bit_cmp_2 (
    .num1(n4bit_cmp_1_greater), .num2(C), .smaller(n4bit_cmp_2_smaller), .greater(n4bit_cmp_2_greater));
  _4bit_cmp u_4bit_cmp_3 (.num1(n4bit_cmp_2_greater), .num2(D), .smaller(n4bit_cmp_3_smaller), .greater(_4));
  _4bit_cmp u_4bit_cmp_4 (
    .num1(n4bit_cmp_1_smaller), .num2(n4bit_cmp_2_smaller), .smaller(n4bit_cmp_4_smaller),
    .greater(n4bit_cmp_4_greater));
  _4bit_cmp u_4bit_cmp_5 (
    .num1(n4bit_cmp_4_greater), .num2(n4bit_cmp_3_smaller), .smaller(n4bit_cmp_5_smaller), .greater(_3));
  _4bit_cmp u_4bit_cmp_6 (.num1(n4bit_cmp_4_smaller), .num2(n4bit_cmp_5_smaller), .smaller(_1), .greater(_2));
endmodule
