// Logisim project CPU.circ as structural Verilog: 7 circuits, main circuit main
module ALU (
  input  [2:0] ALUCtrl,
  input  [31:0] SrcA,
  input  [31:0] SrcB,
  output [31:0] result,
  output Zero
);

  wire AND, comparator_1_lt, multiplexer_4_out, OR, Sub;
  wire [31:0] adder_1_out, and_1_out, bit_extender_1_out, multiplexer_1_out, multiplexer_2_out,
       multiplexer_3_out, not_1_out, not_2_out, not_3_out, or_1_out;

  // Probe on SrcA
  // Probe on SrcB
  assign not_1_out = ~SrcB;  // NOT_Gate not_1, 32 bits wide
  assign not_2_out = ~SrcB;  // NOT_Gate not_2, 32 bits wide
  assign not_3_out = ~SrcB;  // NOT_Gate not_3, 32 bits wide
  Multiplexer #(.width(32), .enable("false")) multiplexer_1 (
    .in0(SrcB), .in1(not_1_out), .out(multiplexer_1_out), .sel(AND));
  Multiplexer #(.width(32), .enable("false")) multiplexer_2 (
    .in0(SrcB), .in1(not_2_out), .out(multiplexer_2_out), .sel(OR));
  Multiplexer #(.width(32), .enable("false")) multiplexer_3 (
    .in0(SrcB), .in1(not_3_out), .out(multiplexer_3_out), .sel(Sub));
  Multiplexer #(.enable("false")) multiplexer_4 (.in0(1'b0), .in1(1'b1), .out(multiplexer_4_out), .sel(Sub));
  Comparator #(.width(32)) comparator_1 (.a(SrcA), .b(SrcB), .eq(Zero), .lt(comparator_1_lt));  // open: gt
  assign and_1_out = SrcA & multiplexer_1_out;  // AND_Gate and_1, 32 bits wide
  assign or_1_out = SrcA | multiplexer_2_out;  // OR_Gate or_1, 32 bits wide
  Adder #(.width(32)) adder_1 (
    .a(SrcA), .b(multiplexer_3_out), .out(adder_1_out), .cin(multiplexer_4_out));  // open: cout
  Decoder #(.select(3), .enable("false")) decoder_1 (
    .out4(AND), .out5(OR), .out6(Sub), .sel(ALUCtrl));  // open: out0, out1, out2, out3, out7
  assign bit_extender_1_out = {{31{1'b0}}, comparator_1_lt};  // Bit_Extender bit_extender_1
  Multiplexer #(.select(3), .width(32), .enable("false")) multiplexer_5 (
    .in0(and_1_out), .in1(or_1_out), .in2(adder_1_out), .in4(and_1_out), .in5(or_1_out), .in6(adder_1_out),
    .in7(bit_extender_1_out), .out(result), .sel(ALUCtrl));  // open: in3
  // Probe on result
endmodule

module main (
  input  Reset
);

  wire and_1_out, Branch, Clk, deco_1_alusrc, deco_1_memtoreg, deco_1_memwrite, deco_1_regdst,
       deco_1_regwrite, jr, Jump, not_1_out, PCtoReg, raWrite, undriven_2, zero;
  wire [1:0] ImmSrc;
  wire [2:0] deco_1_aluctrl;
  wire [4:0] adder_1_out, adder_2_out, alu_1_result_2, multiplexer_1_out, multiplexer_2_out,
       multiplexer_3_out, multiplexer_5_out, multiplexer_8_out, register_1_q, splitter_1__15_11_rd,
       splitter_1__20_16_rt, splitter_1__25_0, splitter_1__25_21_rs, undriven, WriteReg;
  wire [5:0] splitter_1__5_0_funct, splitter_1__31_26_op;
  wire [15:0] splitter_1__15_0;
  wire [20:0] splitter_1__25_0_2;
  wire [26:0] alu_1_result;
  wire [31:0] bit_extender_1_out, bit_extender_2_out, grf_1_rd2, multiplexer_4_out, multiplexer_7_out,
       multiplexer_9_out, PC_plus_4, ram_1_data, RD1, Result, rom_1_data;

  // Probe on adder_2_out
  and and_1 (and_1_out, Branch, zero);
  Multiplexer #(.width(5), .enable("false")) multiplexer_1 (
    .in0(adder_1_out), .in1(adder_2_out), .out(multiplexer_1_out), .sel(and_1_out));
  Multiplexer #(.width(5), .enable("false")) multiplexer_2 (
    .in0(multiplexer_1_out), .in1(multiplexer_3_out), .out(multiplexer_2_out), .sel(Jump));
  Multiplexer #(.width(5), .enable("false")) multiplexer_3 (
    .in0(splitter_1__25_0), .out(multiplexer_3_out), .sel(jr));  // open: in1
  Register #(.width(5)) register_1 (.D(multiplexer_2_out), .Q(register_1_q), .clk(Clk), .clr(Reset));  // open: en
  Adder #(.width(5)) adder_1 (.a(register_1_q), .b(5'b00001), .out(adder_1_out));  // open: cin, cout
  ROM #(.addrWidth(5), .dataWidth(32)) rom_1 (.addr(register_1_q), .data(rom_1_data));  // open: sel
  splitter splitter_1 (
    .in_1(rom_1_data), ._31_26_op(splitter_1__31_26_op), ._25_21_rs(splitter_1__25_21_rs),
    ._20_16_rt(splitter_1__20_16_rt), ._15_11_rd(splitter_1__15_11_rd), ._5_0_funct(splitter_1__5_0_funct),
    ._15_0(splitter_1__15_0), ._25_0({splitter_1__25_0_2, splitter_1__25_0}));  // open: _10_6_shamt
  Deco deco_1 (
    .Opcode(splitter_1__31_26_op), .Funct(splitter_1__5_0_funct), .MemtoReg(deco_1_memtoreg),
    .MemWrite(deco_1_memwrite), .Branch(Branch), .ALUCtrl(deco_1_aluctrl), .ALUSrc(deco_1_alusrc),
    .RegDst(deco_1_regdst), .RegWrite(deco_1_regwrite), .Jump(Jump), .ImmSrc(ImmSrc));
  assign bit_extender_1_out = {{16{splitter_1__15_0[15]}}, splitter_1__15_0};  // Bit_Extender bit_extender_1
  assign bit_extender_2_out = {{16{1'b0}}, splitter_1__15_0};  // Bit_Extender bit_extender_2
  GRF grf_1 (
    .WE3(deco_1_regwrite), .in_2(splitter_1__25_21_rs), .in_3(splitter_1__20_16_rt), .in_4(WriteReg),
    .WD3(Result), .Clr(Reset), .RD1(RD1), .RD2(grf_1_rd2), .CLK(Clk));
  Multiplexer #(.select(2), .width(32), .enable("false")) multiplexer_4 (
    .in0(bit_extender_1_out), .in1(bit_extender_2_out), .in2({splitter_1__15_0, {16{1'b0}}}),
    .out(multiplexer_4_out), .sel(ImmSrc));  // open: in3
  Multiplexer #(.width(5), .enable("false")) multiplexer_5 (
    .in0(splitter_1__20_16_rt), .in1(splitter_1__15_11_rd), .out(multiplexer_5_out), .sel(deco_1_regdst));
  Multiplexer #(.width(5), .enable("false")) multiplexer_6 (
    .in0(multiplexer_5_out), .in1({5{1'b1}}), .out(WriteReg), .sel(raWrite));
  Adder #(.width(5)) adder_2 (.a(bit_extender_1_out[4:0]), .b(adder_1_out), .out(adder_2_out));  // open: cin, cout
  // Probe on deco_1_aluctrl
  Multiplexer #(.width(32), .enable("false")) multiplexer_7 (
    .in0(grf_1_rd2), .in1(multiplexer_4_out), .out(multiplexer_7_out), .sel(deco_1_alusrc));
  ALU alu_1 (
    .ALUCtrl(deco_1_aluctrl), .SrcA(RD1), .SrcB(multiplexer_7_out),
    .result({alu_1_result[26:2], alu_1_result_2, alu_1_result[1:0]}), .Zero(zero));
  Multiplexer #(.width(5), .enable("false")) multiplexer_8 (
    .in0(undriven), .in1({5{1'b1}}), .out(multiplexer_8_out), .sel(undriven_2));
  not not_1 (not_1_out, deco_1_memwrite);
  RAM #(.addrWidth(5), .dataWidth(32), .bus("separate")) ram_1 (
    .addr(alu_1_result_2), .din(grf_1_rd2), .data(ram_1_data), .str(deco_1_memwrite), .clk(Clk),
    .ld(not_1_out));  // open: sel, clr
  Multiplexer #(.width(32), .enable("false")) multiplexer_9 (
    .in0({alu_1_result[26:2], alu_1_result_2, alu_1_result[1:0]}), .in1(ram_1_data), .out(multiplexer_9_out),
    .sel(deco_1_memtoreg));
  Multiplexer #(.width(32), .enable("false")) multiplexer_10 (
    .in0(multiplexer_9_out), .in1(PC_plus_4), .out(Result), .sel(PCtoReg));
  // Probe on Result
  Clock clock_1 (.out(Clk));

  // Notes on the sheet:
  //   contents of rom_1 (hex, n*v repeats v):
  //   20210002 34230005 ac030000 3c03000f ac030001 8100000
  //   25:21
  //   SignImm
  //   15:0
  //   REGDst
  //   REGWrite
  //   20:16
  //   15:11
  //   ALUSrc
  //   ALUCtrl
  //   SrcA
  //   SrcB
  //   ALUResult
  //   MemWrite
  //   MemtoReg
endmodule

module GRF (
  input  WE3,
  input  [4:0] in_2,
  input  [4:0] in_3,
  input  [4:0] in_4,
  input  [31:0] WD3,
  input  Clr,
  input  CLK,
  output [31:0] RD1,
  output [31:0] RD2
);

  wire W1, W2, W3, W4, W5, W6, W7, W8, W9, W10, W11, W12, W13, W14, W15, W16, W17, W18, W19, W20, W21, W22,
       W23, W24, W25, W26, W27, W28, W29, W30, W31;
  wire [31:0] _0, _1, _2, _3, _4, _5, _6, _7, _8, _9, _10, _11, _12, _13, _14, _15, _16, _17, _18, _19, _20,
       _21, _22, _23, _24, _25, _26, _27, _28, _29, _30, _31;

  Decoder #(.select(5), .disabled(0)) decoder_1 (
    .out1(W1), .out2(W2), .out3(W3), .out4(W4), .out5(W5), .out6(W6), .out7(W7), .out8(W8), .out9(W9),
    .out10(W10), .out11(W11), .out12(W12), .out13(W13), .out14(W14), .out15(W15), .out16(W16), .out17(W17),
    .out18(W18), .out19(W19), .out20(W20), .out21(W21), .out22(W22), .out23(W23), .out24(W24), .out25(W25),
    .out26(W26), .out27(W27), .out28(W28), .out29(W29), .out30(W30), .out31(W31), .sel(in_4), .en(WE3));  // open: out0
  Register #(.width(32)) u__0 (.Q(_0), .clk(CLK), .clr(Clr));  // open: D, en
  Register #(.width(32)) u__1 (.D(WD3), .en(W1), .Q(_1), .clk(CLK), .clr(Clr));
  Register #(.width(32)) u__2 (.D(WD3), .en(W2), .Q(_2), .clk(CLK), .clr(Clr));
  Register #(.width(32)) u__3 (.D(WD3), .en(W3), .Q(_3), .clk(CLK), .clr(Clr));
  Register #(.width(32)) u__4 (.D(WD3), .en(W4), .Q(_4), .clk(CLK), .clr(Clr));
  Register #(.width(32)) u__5 (.D(WD3), .en(W5), .Q(_5), .clk(CLK), .clr(Clr));
  Register #(.width(32)) u__6 (.D(WD3), .en(W6), .Q(_6), .clk(CLK), .clr(Clr));
  Register #(.width(32)) u__7 (.D(WD3), .en(W7), .Q(_7), .clk(CLK), .clr(Clr));
  Register #(.width(32)) u__8 (.D(WD3), .en(W8), .Q(_8), .clk(CLK), .clr(Clr));
  Register #(.width(32)) u__9 (.D(WD3), .en(W9), .Q(_9), .clk(CLK), .clr(Clr));
  Register #(.width(32)) u__10 (.D(WD3), .en(W10), .Q(_10), .clk(CLK), .clr(Clr));
  Register #(.width(32)) u__11 (.D(WD3), .en(W11), .Q(_11), .clk(CLK), .clr(Clr));
  Register #(.width(32)) u__12 (.D(WD3), .en(W12), .Q(_12), .clk(CLK), .clr(Clr));
  Register #(.width(32)) u__13 (.D(WD3), .en(W13), .Q(_13), .clk(CLK), .clr(Clr));
  Register #(.width(32)) u__14 (.D(WD3), .en(W14), .Q(_14), .clk(CLK), .clr(Clr));
  Register #(.width(32)) u__15 (.D(WD3), .en(W15), .Q(_15), .clk(CLK), .clr(Clr));
  Register #(.width(32)) u__16 (.D(WD3), .en(W16), .Q(_16), .clk(CLK), .clr(Clr));
  Register #(.width(32)) u__17 (.D(WD3), .en(W17), .Q(_17), .clk(CLK), .clr(Clr));
  Register #(.width(32)) u__18 (.D(WD3), .en(W18), .Q(_18), .clk(CLK), .clr(Clr));
  Register #(.width(32)) u__19 (.D(WD3), .en(W19), .Q(_19), .clk(CLK), .clr(Clr));
  Register #(.width(32)) u__20 (.D(WD3), .en(W20), .Q(_20), .clk(CLK), .clr(Clr));
  Register #(.width(32)) u__21 (.D(WD3), .en(W21), .Q(_21), .clk(CLK), .clr(Clr));
  Register #(.width(32)) u__22 (.D(WD3), .en(W22), .Q(_22), .clk(CLK), .clr(Clr));
  Register #(.width(32)) u__23 (.D(WD3), .en(W23), .Q(_23), .clk(CLK), .clr(Clr));
  Register #(.width(32)) u__24 (.D(WD3), .en(W24), .Q(_24), .clk(CLK), .clr(Clr));
  Register #(.width(32)) u__25 (.D(WD3), .en(W25), .Q(_25), .clk(CLK), .clr(Clr));
  Register #(.width(32)) u__26 (.D(WD3), .en(W26), .Q(_26), .clk(CLK), .clr(Clr));
  Register #(.width(32)) u__27 (.D(WD3), .en(W27), .Q(_27), .clk(CLK), .clr(Clr));
  Register #(.width(32)) u__28 (.D(WD3), .en(W28), .Q(_28), .clk(CLK), .clr(Clr));
  Register #(.width(32)) u__29 (.D(WD3), .en(W29), .Q(_29), .clk(CLK), .clr(Clr));
  Register #(.width(32)) u__30 (.D(WD3), .en(W30), .Q(_30), .clk(CLK), .clr(Clr));
  Register #(.width(32)) u__31 (.D(WD3), .en(W31), .Q(_31), .clk(CLK), .clr(Clr));
  Multiplexer #(.select(5), .width(32), .enable("false")) multiplexer_1 (
    .in0(_0), .in1(_1), .in2(_2), .in3(_3), .in4(_4), .in5(_5), .in6(_6), .in7(_7), .in8(_8), .in9(_9),
    .in10(_10), .in11(_11), .in12(_12), .in13(_13), .in14(_14), .in15(_15), .in16(_16), .in17(_17),
    .in18(_18), .in19(_19), .in20(_20), .in21(_21), .in22(_22), .in23(_23), .in24(_24), .in25(_25),
    .in26(_26), .in27(_27), .in28(_28), .in29(_29), .in30(_30), .in31(_31), .out(RD1), .sel(in_2));
  Multiplexer #(.select(5), .width(32), .enable("false")) multiplexer_2 (
    .in0(_0), .in1(_1), .in2(_2), .in3(_3), .in4(_4), .in5(_5), .in6(_6), .in7(_7), .in8(_8), .in9(_9),
    .in10(_10), .in11(_11), .in12(_12), .in13(_13), .in14(_14), .in15(_15), .in16(_16), .in17(_17),
    .in18(_18), .in19(_19), .in20(_20), .in21(_21), .in22(_22), .in23(_23), .in24(_24), .in25(_25),
    .in26(_26), .in27(_27), .in28(_28), .in29(_29), .in30(_30), .in31(_31), .out(RD2), .sel(in_3));

  // Other names for the same wires on the sheet: A1[4:0] = in_2; A2[4:0] = in_3; A3[4:0] = in_4

  // Notes on the sheet:
  //   MUX1
  //   MUX2
endmodule

// Splitter
module splitter (
  input  [31:0] in_1,
  output [5:0] _31_26_op,
  output [4:0] _25_21_rs,
  output [4:0] _20_16_rt,
  output [4:0] _15_11_rd,
  output [4:0] _10_6_shamt,
  output [5:0] _5_0_funct,
  output [15:0] _15_0,
  output [25:0] _25_0
);


  assign _5_0_funct = in_1[5:0];
  assign _10_6_shamt = in_1[10:6];
  assign _15_0 = in_1[15:0];
  assign _15_11_rd = in_1[15:11];
  assign _20_16_rt = in_1[20:16];
  assign _25_0 = in_1[25:0];
  assign _25_21_rs = in_1[25:21];
  assign _31_26_op = in_1[31:26];
endmodule

module MainDeco (
  input  [5:0] Opcode,
  output RegWrite,
  output RegDst,
  output ALUSrc,
  output Branch,
  output MemWrite,
  output MemtoReg,
  output [2:0] ALUOp,
  output Jump,
  output [1:0] ImmSrc
);

  wire addi_out, not_1_out, not_2_out, not_3_out, not_4_out, not_5_out, not_6_out;

  not not_1 (not_1_out, Opcode[5]);
  not not_2 (not_2_out, Opcode[3]);
  not not_3 (not_3_out, Opcode[4]);
  not not_4 (not_4_out, Opcode[2]);
  not not_5 (not_5_out, Opcode[1]);
  not not_6 (not_6_out, Opcode[0]);
  and R (RegDst, not_1_out, not_3_out, not_2_out, not_4_out, not_5_out, not_6_out);
  and lw (MemtoReg, Opcode[5], not_3_out, not_2_out, not_4_out, Opcode[1], Opcode[0]);
  and sw (MemWrite, Opcode[5], not_3_out, Opcode[3], not_4_out, Opcode[1], Opcode[0]);
  and beq (Branch, not_1_out, not_3_out, not_2_out, Opcode[2], not_5_out, not_6_out);
  and j (Jump, not_1_out, not_3_out, not_2_out, not_4_out, Opcode[1], not_6_out);
  and ori (ImmSrc[0], not_1_out, not_3_out, Opcode[3], Opcode[2], not_5_out, Opcode[0]);
  and lui (ImmSrc[1], not_1_out, not_3_out, Opcode[3], Opcode[2], Opcode[1], Opcode[0]);
  and addi (addi_out, not_1_out, not_3_out, Opcode[3], not_4_out, not_5_out, not_6_out);
  or or_1 (RegWrite, RegDst, addi_out, ImmSrc[1], ImmSrc[0], MemtoReg);
  or or_2 (ALUSrc, MemtoReg, addi_out, ImmSrc[1], ImmSrc[0], MemWrite);
  buf or_3 (ALUOp[2], Branch);  // OR_Gate
  or or_4 (ALUOp[1], MemWrite, RegDst, MemtoReg, Branch, addi_out, ImmSrc[1]);
  or or_5 (ALUOp[0], RegDst, ImmSrc[0]);

  // Other names for the same wires on the sheet: _0 = Opcode[0]; _1 = Opcode[1]; _2 = Opcode[2]; _3 = Opcode[3];
  //   _4 = Opcode[4]; _5 = Opcode[5]
endmodule

module ALUDeco (
  input  [2:0] ALUOp,
  input  [5:0] Funct,
  output [2:0] ALUCtrl
);

  wire add, add1, \and , not_1_out, not_2_out, not_3_out, not_4_out, not_5_out, not_6_out, not_7_out, \or ,
       slt, Src, sub, sub1;
  wire [2:0] or_6_out;

  not not_1 (not_1_out, ALUOp[2]);
  and and_1 (Src, not_1_out, ALUOp[1], ALUOp[0]);
  not not_2 (not_2_out, Funct[5]);
  not not_3 (not_3_out, Funct[3]);
  not not_4 (not_4_out, Funct[4]);
  not not_5 (not_5_out, Funct[2]);
  not not_6 (not_6_out, Funct[1]);
  not not_7 (not_7_out, Funct[0]);
  and u_add (add1, Funct[5], not_4_out, not_3_out, not_5_out, not_6_out);
  and u_sub (sub1, Funct[5], not_4_out, not_3_out, not_5_out, Funct[1]);
  and and_2 (\and , Funct[5], not_4_out, not_3_out, Funct[2], not_6_out, not_7_out);
  and u_or (\or , Funct[5], not_4_out, not_3_out, Funct[2], not_6_out, Funct[0]);
  and u_slt (slt, Funct[5], not_4_out, Funct[3], not_5_out, Funct[1], not_7_out);
  buf or_2 (add, add1);  // OR_Gate
  buf or_3 (sub, sub1);  // OR_Gate
  or or_4 (or_6_out[2], sub, slt);
  or or_5 (or_6_out[1], sub, slt, add);
  or or_6 (or_6_out[0], \or , slt);
  Multiplexer #(.width(3), .enable("false")) multiplexer_1 (.in0(ALUOp), .in1(or_6_out), .out(ALUCtrl), .sel(Src));

  // Other names for the same wires on the sheet: _0 = Funct[0]; _1 = Funct[1]; _2 = Funct[2]; _3 = Funct[3];
  //   _4 = Funct[4]; _5 = Funct[5]
endmodule

// Ctrler
module Deco (
  input  [5:0] Opcode,
  input  [5:0] Funct,
  output MemtoReg,
  output MemWrite,
  output Branch,
  output [2:0] ALUCtrl,
  output ALUSrc,
  output RegDst,
  output RegWrite,
  output Jump,
  output [1:0] ImmSrc
);

  wire [2:0] maindeco_1_aluop;

  MainDeco maindeco_1 (
    .Opcode(Opcode), .RegWrite(RegWrite), .RegDst(RegDst), .ALUSrc(ALUSrc), .Branch(Branch),
    .MemWrite(MemWrite), .MemtoReg(MemtoReg), .ALUOp(maindeco_1_aluop), .Jump(Jump), .ImmSrc(ImmSrc));
  // Probe on maindeco_1_aluop
  ALUDeco aludeco_1 (.ALUOp(maindeco_1_aluop), .Funct(Funct), .ALUCtrl(ALUCtrl));
endmodule
