// Logisim project fib.circ as structural Verilog: 1 circuit, main circuit main
module main (
  input  [2:0] in_1,
  output [3:0] out_2
);

  wire clock_1_out, comparator_1_gt, comparator_2_eq, comparator_3_eq, comparator_3_gt, comparator_3_lt,
       not_1_out;
  wire [1:0] priority_encoder_1_out;
  wire [2:0] counter_1_q;
  wire [3:0] adder_1_out, bit_extender_1_out, controlled_buffer_1_out, L1_q, L2_q, multiplexer_1_out,
       multiplexer_2_out;

  Clock clock_1 (.out(clock_1_out));
  Comparator #(.width(3), .mode("unsigned")) comparator_1 (.a(in_1), .b(3'b001), .gt(comparator_1_gt));  // open: eq, lt
  Counter #(.width(3), .max('h7), .ongoal("stay")) counter_1 (
    .Q(counter_1_q), .clk(clock_1_out));  // open: load, D, count, carry, clr
  not not_1 (not_1_out, comparator_1_gt);
  Register #(.width(4)) L1 (.D(multiplexer_1_out), .Q(L1_q), .clk(clock_1_out));  // open: en, clr
  Comparator #(.width(3), .mode("unsigned")) comparator_2 (
    .a(counter_1_q), .b(in_1), .eq(comparator_2_eq));  // open: gt, lt
  Register #(.width(4)) L2 (.D(L1_q), .Q(L2_q), .clk(clock_1_out));  // open: en, clr
  Adder #(.width(4)) adder_1 (.a(L2_q), .b(L1_q), .out(adder_1_out));  // open: cin, cout
  assign bit_extender_1_out = {{1{1'b0}}, in_1};  // Bit_Extender bit_extender_1
  assign controlled_buffer_1_out = not_1_out ? bit_extender_1_out : 4'bz;  // Controlled_Buffer controlled_buffer_1
  Comparator #(.width(3), .mode("unsigned")) comparator_3 (
    .a(counter_1_q), .b(3'b001), .gt(comparator_3_gt), .eq(comparator_3_eq), .lt(comparator_3_lt));
  Multiplexer #(.select(2), .width(4)) multiplexer_1 (
    .in0(adder_1_out), .in1(4'b0001), .in2(4'b0000), .out(multiplexer_1_out), .sel(priority_encoder_1_out));  // open: in3, en
  // Probe on priority_encoder_1_out
  Priority_Encoder #(.select(2)) priority_encoder_1 (
    .in0(comparator_3_gt), .in1(comparator_3_eq), .in2(comparator_3_lt), .out(priority_encoder_1_out));  // open: in3, gs, en_out, en_in
  Multiplexer #(.width(4)) multiplexer_2 (
    .in0(4'b0000), .in1(multiplexer_1_out), .out(multiplexer_2_out), .sel(comparator_2_eq));  // open: en
  Multiplexer #(.width(4)) multiplexer_3 (
    .in0(multiplexer_2_out), .in1(controlled_buffer_1_out), .out(out_2), .sel(not_1_out));  // open: en

  // Notes on the sheet:
  //   L1+L2
endmodule
