// Logisim project fib2.circ as structural Verilog: 2 circuits, main circuit main
module main (
  input  [2:0] in_1,
  output [3:0] out_2
);

  wire clock_1_out, comparator_1_eq, comparator_1_gt, comparator_1_lt, comparator_2_gt, comparator_3_eq,
       comparator_3_gt, comparator_3_lt, not_1_out;
  wire [1:0] priority_encoder_1_out, priority_encoder_2_out;
  wire [3:0] adder_1_out, bit_extender_1_out, controlled_buffer_1_out, counter_1_q, L1_q, L2_2_q, L2_q,
       multiplexer_1_out, multiplexer_2_out;

  assign bit_extender_1_out = {{1{1'b0}}, in_1};  // Bit_Extender bit_extender_1
  Clock clock_1 (.out(clock_1_out));
  Counter #(.width(4), .max('hf), .ongoal("stay")) counter_1 (
    .Q(counter_1_q), .clk(clock_1_out));  // open: load, D, count, carry, clr
  Register #(.width(4)) L1 (.D(multiplexer_1_out), .Q(L1_q), .clk(clock_1_out));  // open: en, clr
  Comparator #(.width(4), .mode("unsigned")) comparator_1 (
    .a(counter_1_q), .b(bit_extender_1_out), .gt(comparator_1_gt), .eq(comparator_1_eq), .lt(comparator_1_lt));
  not not_1 (not_1_out, comparator_2_gt);
  Comparator #(.width(4), .mode("unsigned")) comparator_2 (
    .a(bit_extender_1_out), .b(4'b0001), .gt(comparator_2_gt));  // open: eq, lt
  Register #(.width(4)) L2 (.D(L1_q), .Q(L2_q), .clk(clock_1_out));  // open: en, clr
  Priority_Encoder #(.select(2)) priority_encoder_1 (
    .in0(comparator_1_gt), .in1(comparator_1_eq), .in2(comparator_1_lt), .out(priority_encoder_1_out));  // open: in3, gs, en_out, en_in
  // Probe on priority_encoder_1_out
  Adder #(.width(4)) adder_1 (.a(L2_q), .b(L1_q), .out(adder_1_out));  // open: cin, cout
  assign controlled_buffer_1_out = not_1_out ? bit_extender_1_out : 4'bz;  // Controlled_Buffer controlled_buffer_1
  Priority_Encoder #(.select(2)) priority_encoder_2 (
    .in0(comparator_3_gt), .in1(comparator_3_eq), .in2(comparator_3_lt), .out(priority_encoder_2_out));  // open: in3, gs, en_out, en_in
  Comparator #(.width(4), .mode("unsigned")) comparator_3 (
    .a(counter_1_q), .b(4'b0001), .gt(comparator_3_gt), .eq(comparator_3_eq), .lt(comparator_3_lt));
  Multiplexer #(.select(2), .width(4)) multiplexer_1 (
    .in0(adder_1_out), .in1(4'b0001), .in2(4'b0000), .out(multiplexer_1_out), .sel(priority_encoder_2_out));  // open: in3, en
  // Probe on priority_encoder_2_out
  // Probe on multiplexer_2_out
  Register #(.width(4)) L2_2 (.D(multiplexer_2_out), .Q(L2_2_q), .clk(clock_1_out));  // open: en, clr
  Multiplexer #(.select(2), .width(4)) multiplexer_2 (
    .in0(L2_2_q), .in1(multiplexer_1_out), .in2(4'b0000), .out(multiplexer_2_out),
    .sel(priority_encoder_1_out));  // open: in3, en
  Multiplexer #(.width(4)) multiplexer_3 (
    .in0(multiplexer_2_out), .in1(controlled_buffer_1_out), .out(out_2), .sel(not_1_out));  // open: en

  // Notes on the sheet:
  //   L1+L2
endmodule

module test (
  output [3:0] out_1,
  output out_2
);

  wire clock_1_out;
  wire [3:0] main_1_out_2;

  main main_1 (.in_1(3'b111), .out_2(main_1_out_2));
  Counter #(.width(3), .max('h7)) counter_1 (.carry(out_2), .clk(clock_1_out));  // open: load, D, count, Q, clr
  Clock clock_1 (.out(clock_1_out));
  Register #(.width(4)) register_1 (.D(main_1_out_2), .Q(out_1), .clk(out_2));  // open: en, clr
endmodule
