// Logisim project mfr.circ as structural Verilog: 2 circuits, main circuit mod5
module mod5 (
  input  in_1,
  output out_2,
  output out_3,
  output out_4,
  output out_5,
  output out_6
);

  wire and_1_out, and_2_out, and_3_out, and_4_out, clock_1_out, nor_1_out, not_1_out, not_2_out, not_3_out,
       or_1_out, or_2_out, register_1_q, register_2_q, register_3_q, register_4_q;

  Clock clock_1 (.out(clock_1_out));
  Register #(.width(1)) register_1 (.D(out_3), .Q(register_1_q), .clk(clock_1_out));  // open: en, clr
  Register #(.width(1)) register_2 (.D(out_4), .Q(register_2_q), .clk(clock_1_out));  // open: en, clr
  Register #(.width(1)) register_3 (.D(out_5), .Q(register_3_q), .clk(clock_1_out));  // open: en, clr
  Register #(.width(1)) register_4 (.D(out_6), .Q(register_4_q), .clk(clock_1_out));  // open: en, clr
  nor nor_1 (nor_1_out, register_3_q, register_2_q, register_1_q, register_4_q);
  not not_1 (not_1_out, in_1);
  not not_2 (not_2_out, in_1);
  or or_1 (or_1_out, register_1_q, register_4_q);
  or or_2 (or_2_out, register_2_q, register_3_q);
  not not_3 (not_3_out, in_1);
  and and_1 (and_1_out, in_1, nor_1_out);
  and and_2 (and_2_out, nor_1_out, not_1_out);
  and and_3 (and_3_out, not_2_out, or_1_out);
  and and_4 (and_4_out, in_1, or_1_out);
  and and_5 (out_5, in_1, or_2_out);
  and and_6 (out_6, or_2_out, not_3_out);
  or or_3 (out_3, and_2_out, and_3_out);
  or or_4 (out_4, and_1_out, and_4_out);

  assign out_2 = 1'b0;
endmodule

module test (
  output out_1,
  output out_2,
  output out_3,
  output out_4,
  output out_5,
  output out_6,
  output out_7
);

  wire clock_1_out;
  wire [3:0] counter_1_q;

  Clock clock_1 (.out(clock_1_out));
  Counter #(.width(4), .max('hf)) counter_1 (
    .Q(counter_1_q), .carry(out_7), .clk(clock_1_out));  // open: load, D, count, clr
  ROM #(.addrWidth(4), .dataWidth(1)) rom_1 (.addr(counter_1_q), .data(out_1));  // open: sel
  mod5 mod5_1 (.in_1(out_1), .out_2(out_2), .out_3(out_3), .out_4(out_4), .out_5(out_5), .out_6(out_6));

  // Notes on the sheet:
  //   contents of rom_1 (hex, n*v repeats v):
  //   1 1 0 0 1 0 0 1 0 0 1 0 0 1
endmodule
