// Logisim project mod5.circ as structural Verilog: 3 circuits, main circuit 5points
module _5points (
  input  In,
  output S0,
  output S1,
  output S2,
  output S3,
  output S4
);

  wire and_1_out, and_2_out, and_3_out, and_4_out, and_5_out, and_6_out, and_7_out, and_8_out, and_9_out,
       and_10_out, clock_1_out, or_1_out, S1_q, S2_q, xor_1_out, xor_2_out, xor_3_out, xor_4_out;

  and and_1 (and_1_out, ~S0, ~S1_q, ~S4, ~In);  // AND_Gate
  and and_2 (and_2_out, ~In, ~S0, ~S2_q, ~S3);  // AND_Gate
  and and_3 (and_3_out, In, ~S0, ~S2_q, ~S3);  // AND_Gate
  and and_4 (and_4_out, ~S0, ~S1_q, ~S4, In);  // AND_Gate
  xor xor_1 (xor_1_out, S1_q, S4);
  xor xor_2 (xor_2_out, S1_q, S4);
  and and_5 (and_5_out, and_2_out, xor_1_out);
  and and_6 (and_6_out, ~In, ~S0, ~S1_q, ~S2_q, ~S3, ~S4);  // AND_Gate
  and and_7 (and_7_out, and_3_out, xor_2_out);
  and and_8 (and_8_out, In, ~S4, ~S3, ~S2_q, ~S1_q, ~S0);  // AND_Gate
  Clock clock_1 (.out(clock_1_out));
  xor xor_3 (xor_3_out, S2_q, S3);
  xor xor_4 (xor_4_out, S3, S2_q);
  or or_1 (or_1_out, and_7_out, and_8_out);
  and and_9 (and_9_out, and_4_out, xor_3_out);
  and and_10 (and_10_out, and_1_out, xor_4_out);
  Register #(.width(1)) u_S0 (.Q(S0), .clk(clock_1_out));  // open: D, en, clr
  Register #(.width(1)) u_S1 (.D(and_5_out), .Q(S1_q), .clk(clock_1_out));  // open: en, clr
  Register #(.width(1)) u_S2 (.D(or_1_out), .Q(S2_q), .clk(clock_1_out));  // open: en, clr
  Register #(.width(1)) u_S3 (.D(and_9_out), .Q(S3), .clk(clock_1_out));  // open: en, clr
  Register #(.width(1)) u_S4 (.D(and_10_out), .Q(S4), .clk(clock_1_out));  // open: en, clr
  or or_2 (S1, S1_q, and_6_out);
  or or_3 (S2, S2_q, and_8_out);
endmodule

module test (
  output out_1,
  output out_2,
  output out_3,
  output out_4,
  output out_5,
  output out_6,
  output out_7
);

  wire clock_1_out;
  wire [3:0] counter_1_q;

  Clock clock_1 (.out(clock_1_out));
  Counter #(.width(4), .max('hf)) counter_1 (
    .Q(counter_1_q), .carry(out_7), .clk(clock_1_out));  // open: load, D, count, clr
  ROM #(.addrWidth(4), .dataWidth(1)) rom_1 (.addr(counter_1_q), .data(out_1));  // open: sel
  mod5 mod5_1 (.In(out_1), .S0(out_2), .S1(out_3), .S2(out_4), .S3(out_5), .S4(out_6));

  // Notes on the sheet:
  //   contents of rom_1 (hex, n*v repeats v):
  //   1 1 0 0 1 0 0 1 0 0 1 0 0 1
endmodule

module mod5 (
  input  In,
  output S0,
  output S1,
  output S2,
  output S3,
  output S4
);

  wire and_1_out, and_2_out, and_3_out, and_4_out, and_5_out, and_6_out, and_7_out, and_8_out, and_9_out,
       and_10_out, clock_1_out, nor_1_out, S1_q, S2_q, S3_q, S4_q;

  Clock clock_1 (.out(clock_1_out));
  Register #(.width(1)) u_S1 (.D(S1), .Q(S1_q), .clk(clock_1_out));  // open: en, clr
  Register #(.width(1)) u_S2 (.D(S2), .Q(S2_q), .clk(clock_1_out));  // open: en, clr
  Register #(.width(1)) u_S3 (.D(S3), .Q(S3_q), .clk(clock_1_out));  // open: en, clr
  Register #(.width(1)) u_S4 (.D(S4), .Q(S4_q), .clk(clock_1_out));  // open: en, clr
  nor nor_1 (nor_1_out, S1_q, S2_q, S3_q, S3_q);
  and and_1 (and_1_out, ~In, S1_q);  // AND_Gate
  and and_2 (and_2_out, ~In, S4_q);  // AND_Gate
  and and_3 (and_3_out, ~In, nor_1_out);  // AND_Gate
  and and_4 (and_4_out, nor_1_out, In);
  and and_5 (and_5_out, In, S1_q);
  and and_6 (and_6_out, In, S4_q);
  and and_7 (and_7_out, In, S2_q);
  and and_8 (and_8_out, In, S3_q);
  and and_9 (and_9_out, ~In, S2_q);  // AND_Gate
  and and_10 (and_10_out, ~In, S3_q);  // AND_Gate
  or or_1 (S1, and_1_out, and_2_out, and_3_out);
  or or_2 (S2, and_4_out, and_5_out, and_6_out);
  or or_3 (S3, and_7_out, and_8_out);
  or or_4 (S4, and_9_out, and_10_out);

  assign S0 = 1'b0;
endmodule
