// Logisim project fsm.circ as structural Verilog: 3 circuits, main circuit Logic
module Logic (
  input  [2:0] Q,
  input  [1:0] In,
  output [2:0] Out,
  output Z
);

  wire and_2_out, and_3_out, and_4_out, and_5_out, and_6_out, and_7_out, and_8_out, and_9_out, not_1_out,
       not_2_out, not_3_out, not_4_out, not_5_out, not_6_out, not_7_out, not_8_out, not_9_out, not_10_out,
       not_11_out, not_12_out, not_13_out, not_14_out, not_15_out, not_16_out, not_17_out, not_18_out,
       not_19_out;

  not not_1 (not_1_out, In[0]);
  not not_2 (not_2_out, Q[1]);
  not not_3 (not_3_out, In[1]);
  not not_4 (not_4_out, Q[1]);
  not not_5 (not_5_out, In[0]);
  not not_6 (not_6_out, Q[0]);
  not not_7 (not_7_out, In[1]);
  not not_8 (not_8_out, Q[0]);
  not not_9 (not_9_out, In[0]);
  not not_10 (not_10_out, Q[1]);
  not not_11 (not_11_out, Q[0]);
  not not_12 (not_12_out, In[1]);
  not not_13 (not_13_out, In[1]);
  not not_14 (not_14_out, Q[2]);
  not not_15 (not_15_out, In[0]);
  and and_1 (Out[2], Q[1], Q[0], not_1_out);
  and and_2 (and_2_out, not_2_out, Q[0], not_3_out);
  and and_3 (and_3_out, not_4_out, Q[0], not_5_out);
  and and_4 (and_4_out, Q[1], not_6_out, not_7_out);
  and and_5 (and_5_out, Q[1], not_8_out, not_9_out);
  and and_6 (and_6_out, not_10_out, not_11_out, not_12_out, In[0]);
  not not_16 (not_16_out, Q[1]);
  and and_7 (and_7_out, not_16_out, Q[0], not_17_out);
  not not_17 (not_17_out, In[0]);
  not not_18 (not_18_out, Q[0]);
  and and_8 (and_8_out, Q[1], not_18_out, not_19_out);
  not not_19 (not_19_out, In[0]);
  and and_9 (and_9_out, Q[1], Q[0], not_13_out, In[0]);
  and and_10 (Z, not_14_out, Q[1], Q[0], not_15_out);
  or or_1 (Out[1], and_2_out, and_3_out, and_4_out, and_5_out);
  or or_2 (Out[0], and_6_out, and_7_out, and_8_out, and_9_out);
endmodule

module fsm (
  input  [1:0] In,
  input  CLR,
  output Z
);

  wire clock_1_out;
  wire [2:0] logic_1_out, multiplexer_1_out, register_1_q;

  Multiplexer #(.width(3), .enable("false")) multiplexer_1 (
    .in0(logic_1_out), .in1(3'b000), .out(multiplexer_1_out), .sel(CLR));
  Clock clock_1 (.out(clock_1_out));
  Register #(.width(3)) register_1 (.D(multiplexer_1_out), .Q(register_1_q), .clk(clock_1_out));  // open: en, clr
  // Probe on register_1_q
  Logic logic_1 (.Q(register_1_q), .In(In), .Out(logic_1_out), .Z(Z));
  // Probe on logic_1_out
endmodule

module L (
  input  Q1,
  input  Q2,
  input  Q3,
  input  In1,
  input  In2,
  output O1,
  output O2,
  output O3,
  output Z
);

  wire and_2_out, and_3_out, and_4_out, and_5_out, and_6_out, and_7_out, and_8_out, and_9_out, not_1_out,
       not_2_out, not_3_out, not_4_out, not_5_out, not_6_out, not_7_out, not_8_out, not_9_out, not_10_out,
       not_11_out, not_12_out, not_13_out, not_14_out, not_15_out, not_16_out, not_17_out, not_18_out,
       not_19_out;

  not not_1 (not_1_out, In2);
  not not_2 (not_2_out, Q2);
  not not_3 (not_3_out, In1);
  not not_4 (not_4_out, Q2);
  not not_5 (not_5_out, In2);
  not not_6 (not_6_out, Q3);
  not not_7 (not_7_out, In1);
  not not_8 (not_8_out, Q3);
  not not_9 (not_9_out, In2);
  not not_10 (not_10_out, Q2);
  not not_11 (not_11_out, Q3);
  not not_12 (not_12_out, In1);
  not not_13 (not_13_out, Q2);
  not not_14 (not_14_out, In2);
  not not_15 (not_15_out, Q3);
  not not_16 (not_16_out, In2);
  not not_17 (not_17_out, In1);
  not not_18 (not_18_out, Q1);
  not not_19 (not_19_out, In2);
  and and_1 (O1, Q2, Q3, not_1_out);
  and and_2 (and_2_out, not_2_out, Q3, not_3_out);
  and and_3 (and_3_out, not_4_out, Q3, not_5_out);
  and and_4 (and_4_out, Q2, not_6_out, not_7_out);
  and and_5 (and_5_out, Q2, not_8_out, not_9_out);
  and and_6 (and_6_out, not_10_out, not_11_out, not_12_out, In2);
  and and_7 (and_7_out, not_13_out, Q3, not_14_out);
  and and_8 (and_8_out, Q2, not_15_out, not_16_out);
  and and_9 (and_9_out, Q2, Q3, not_17_out, In2);
  and and_10 (Z, not_18_out, Q2, Q3, not_19_out);
  or or_1 (O2, and_2_out, and_3_out, and_4_out, and_5_out);
  or or_2 (O3, and_6_out, and_7_out, and_8_out, and_9_out);
endmodule
